// Logisim project Datapath.circ as structural Verilog: 5 circuits, main circuit main
module main (
  input  [2:0] ALU_Sel,
  input  [1:0] WB_Sel,
  input  ASel,
  input  PC_Sel,
  input  in_5,
  input  BSel,
  input  [1:0] in_7,
  output out_8,
  output out_9
);

  wire clock_1_out;
  wire [16:0] rom_1_data;
  wire [24:7] rom_1_data_2;
  wire [31:0] adder_1_out, adder_2_out, alu_1_result, immediate_generation_1_imm, multiplexer_1_out,
       multiplexer_2_out, multiplexer_3_out, multiplexer_4_out, PC_q, register_file_1_dataa,
       register_file_1_datab;

  Multiplexer #(.width(32)) multiplexer_1 (
    .in0(adder_1_out), .in1(adder_2_out), .out(multiplexer_1_out), .sel(PC_Sel));  // open: en
  Register #(.width(32)) PC (.D(multiplexer_1_out), .Q(PC_q), .clk(clock_1_out));  // open: en, clr
  Clock clock_1 (.out(clock_1_out));
  Adder #(.width(32)) adder_1 (.a(PC_q), .b(32'h4), .out(adder_1_out));  // open: cin, cout
  ROM #(.addrWidth(4), .dataWidth(32)) rom_1 (
    .addr(PC_q[5:2]),
    .data({rom_1_data[16:10], rom_1_data_2[24:15], rom_1_data[9:7], rom_1_data_2[11:7], rom_1_data[6:0]}));  // open: sel
  // Probe on multiplexer_4_out
  Register_File register_file_1 (
    .DataD(multiplexer_4_out), .AddrD(rom_1_data_2[11:7]), .DataA(register_file_1_dataa),
    .AddrA(rom_1_data_2[19:15]), .DataB(register_file_1_datab), .AddrB(rom_1_data_2[24:20]), .RegWEn(in_5));
  Immediate_Generation immediate_generation_1 (
    .Imm(immediate_generation_1_imm),
    .inst({rom_1_data[16:10], rom_1_data_2[24:15], rom_1_data[9:7], rom_1_data_2[11:7], rom_1_data[6:0]}),
    .Imm_Sel(in_7));
  Multiplexer #(.width(32)) multiplexer_2 (
    .in0(register_file_1_dataa), .in1(PC_q), .out(multiplexer_2_out), .sel(ASel));  // open: en
  Multiplexer #(.width(32)) multiplexer_3 (
    .in0(register_file_1_datab), .in1(immediate_generation_1_imm), .out(multiplexer_3_out), .sel(BSel));  // open: en
  Adder #(.width(32)) adder_2 (.a(PC_q), .b(immediate_generation_1_imm), .out(adder_2_out));  // open: cin, cout
  // Probe on alu_1_result
  ALU alu_1 (
    .A(multiplexer_2_out), .B(multiplexer_3_out), .Result(alu_1_result), .ALU_Sel(ALU_Sel));  // open: zero_flag
  Branch_Comp branch_comp_1 (
    .Data_A(register_file_1_dataa), .Data_B(register_file_1_datab), .Br_Eq(out_8), .Br_LT(out_9));
  Multiplexer #(.select(2), .width(32)) multiplexer_4 (
    .in0(alu_1_result), .in1(adder_1_out), .in2({32{1'b0}}), .out(multiplexer_4_out), .sel(WB_Sel));  // open: in3, en

  // Notes on the sheet:
  //   PC MUX
  //        PC+4
  //            ROM
  //   contents of rom_1 (hex, n*v repeats v):
  //   700293 500313 6283b3 40628433 38063 8384b3
endmodule

module Register_File (
  input  [31:0] DataD,
  input  RegWEn,
  input  [4:0] AddrA,
  input  [4:0] AddrD,
  input  [4:0] AddrB,
  output [31:0] DataA,
  output [31:0] DataB
);

  wire clock_1_out, demultiplexer_1_out0, demultiplexer_1_out1, demultiplexer_1_out2, demultiplexer_1_out3,
       demultiplexer_1_out4, demultiplexer_1_out5, demultiplexer_1_out6, demultiplexer_1_out7,
       demultiplexer_1_out8, demultiplexer_1_out9, demultiplexer_1_out10, demultiplexer_1_out11,
       demultiplexer_1_out12, demultiplexer_1_out13, demultiplexer_1_out14, demultiplexer_1_out15,
       demultiplexer_1_out16, demultiplexer_1_out17, demultiplexer_1_out18, demultiplexer_1_out19,
       demultiplexer_1_out20, demultiplexer_1_out21, demultiplexer_1_out22, demultiplexer_1_out23,
       demultiplexer_1_out24, demultiplexer_1_out25, demultiplexer_1_out26, demultiplexer_1_out27,
       demultiplexer_1_out28, demultiplexer_1_out29, demultiplexer_1_out30, demultiplexer_1_out31;
  wire [31:0] register_1_q, register_2_q, register_3_q, register_4_q, register_5_q, register_6_q,
       register_7_q, register_8_q, register_9_q, register_10_q, register_11_q, register_12_q, register_13_q,
       register_14_q, register_15_q, register_16_q, register_17_q, register_18_q, register_19_q,
       register_20_q, register_21_q, register_22_q, register_23_q, register_24_q, register_25_q,
       register_26_q, register_27_q, register_28_q, register_29_q, register_30_q, register_31_q,
       register_32_q;

  Demultiplexer #(.select(5)) demultiplexer_1 (
    .out0(demultiplexer_1_out0), .out1(demultiplexer_1_out1), .out2(demultiplexer_1_out2),
    .out3(demultiplexer_1_out3), .out4(demultiplexer_1_out4), .out5(demultiplexer_1_out5),
    .out6(demultiplexer_1_out6), .out7(demultiplexer_1_out7), .out8(demultiplexer_1_out8),
    .out9(demultiplexer_1_out9), .out10(demultiplexer_1_out10), .out11(demultiplexer_1_out11),
    .out12(demultiplexer_1_out12), .out13(demultiplexer_1_out13), .out14(demultiplexer_1_out14),
    .out15(demultiplexer_1_out15), .out16(demultiplexer_1_out16), .out17(demultiplexer_1_out17),
    .out18(demultiplexer_1_out18), .out19(demultiplexer_1_out19), .out20(demultiplexer_1_out20),
    .out21(demultiplexer_1_out21), .out22(demultiplexer_1_out22), .out23(demultiplexer_1_out23),
    .out24(demultiplexer_1_out24), .out25(demultiplexer_1_out25), .out26(demultiplexer_1_out26),
    .out27(demultiplexer_1_out27), .out28(demultiplexer_1_out28), .out29(demultiplexer_1_out29),
    .out30(demultiplexer_1_out30), .out31(demultiplexer_1_out31), .in(RegWEn), .sel(AddrD));  // open: en
  Clock clock_1 (.out(clock_1_out));
  Register #(.width(32)) register_1 (
    .D(DataD), .en(demultiplexer_1_out0), .Q(register_1_q), .clk(clock_1_out));  // open: clr
  Register #(.width(32)) register_2 (
    .D(DataD), .en(demultiplexer_1_out1), .Q(register_2_q), .clk(clock_1_out));  // open: clr
  Register #(.width(32)) register_3 (
    .D(DataD), .en(demultiplexer_1_out2), .Q(register_3_q), .clk(clock_1_out));  // open: clr
  Register #(.width(32)) register_4 (
    .D(DataD), .en(demultiplexer_1_out3), .Q(register_4_q), .clk(clock_1_out));  // open: clr
  Register #(.width(32)) register_5 (
    .D(DataD), .en(demultiplexer_1_out4), .Q(register_5_q), .clk(clock_1_out));  // open: clr
  Register #(.width(32)) register_6 (
    .D(DataD), .en(demultiplexer_1_out5), .Q(register_6_q), .clk(clock_1_out));  // open: clr
  Register #(.width(32)) register_7 (
    .D(DataD), .en(demultiplexer_1_out6), .Q(register_7_q), .clk(clock_1_out));  // open: clr
  Register #(.width(32)) register_8 (
    .D(DataD), .en(demultiplexer_1_out7), .Q(register_8_q), .clk(clock_1_out));  // open: clr
  Register #(.width(32)) register_9 (
    .D(DataD), .en(demultiplexer_1_out8), .Q(register_9_q), .clk(clock_1_out));  // open: clr
  Register #(.width(32)) register_10 (
    .D(DataD), .en(demultiplexer_1_out9), .Q(register_10_q), .clk(clock_1_out));  // open: clr
  Register #(.width(32)) register_11 (
    .D(DataD), .en(demultiplexer_1_out10), .Q(register_11_q), .clk(clock_1_out));  // open: clr
  Register #(.width(32)) register_12 (
    .D(DataD), .en(demultiplexer_1_out11), .Q(register_12_q), .clk(clock_1_out));  // open: clr
  Register #(.width(32)) register_13 (
    .D(DataD), .en(demultiplexer_1_out12), .Q(register_13_q), .clk(clock_1_out));  // open: clr
  Register #(.width(32)) register_14 (
    .D(DataD), .en(demultiplexer_1_out13), .Q(register_14_q), .clk(clock_1_out));  // open: clr
  Register #(.width(32)) register_15 (
    .D(DataD), .en(demultiplexer_1_out14), .Q(register_15_q), .clk(clock_1_out));  // open: clr
  Register #(.width(32)) register_16 (
    .D(DataD), .en(demultiplexer_1_out15), .Q(register_16_q), .clk(clock_1_out));  // open: clr
  Register #(.width(32)) register_17 (
    .D(DataD), .en(demultiplexer_1_out16), .Q(register_17_q), .clk(clock_1_out));  // open: clr
  Register #(.width(32)) register_18 (
    .D(DataD), .en(demultiplexer_1_out17), .Q(register_18_q), .clk(clock_1_out));  // open: clr
  Register #(.width(32)) register_19 (
    .D(DataD), .en(demultiplexer_1_out18), .Q(register_19_q), .clk(clock_1_out));  // open: clr
  Register #(.width(32)) register_20 (
    .D(DataD), .en(demultiplexer_1_out19), .Q(register_20_q), .clk(clock_1_out));  // open: clr
  Register #(.width(32)) register_21 (
    .D(DataD), .en(demultiplexer_1_out20), .Q(register_21_q), .clk(clock_1_out));  // open: clr
  Register #(.width(32)) register_22 (
    .D(DataD), .en(demultiplexer_1_out21), .Q(register_22_q), .clk(clock_1_out));  // open: clr
  Register #(.width(32)) register_23 (
    .D(DataD), .en(demultiplexer_1_out22), .Q(register_23_q), .clk(clock_1_out));  // open: clr
  Register #(.width(32)) register_24 (
    .D(DataD), .en(demultiplexer_1_out23), .Q(register_24_q), .clk(clock_1_out));  // open: clr
  Register #(.width(32)) register_25 (
    .D(DataD), .en(demultiplexer_1_out24), .Q(register_25_q), .clk(clock_1_out));  // open: clr
  Register #(.width(32)) register_26 (
    .D(DataD), .en(demultiplexer_1_out25), .Q(register_26_q), .clk(clock_1_out));  // open: clr
  Register #(.width(32)) register_27 (
    .D(DataD), .en(demultiplexer_1_out26), .Q(register_27_q), .clk(clock_1_out));  // open: clr
  Register #(.width(32)) register_28 (
    .D(DataD), .en(demultiplexer_1_out27), .Q(register_28_q), .clk(clock_1_out));  // open: clr
  Register #(.width(32)) register_29 (
    .D(DataD), .en(demultiplexer_1_out28), .Q(register_29_q), .clk(clock_1_out));  // open: clr
  Register #(.width(32)) register_30 (
    .D(DataD), .en(demultiplexer_1_out29), .Q(register_30_q), .clk(clock_1_out));  // open: clr
  Register #(.width(32)) register_31 (
    .D(DataD), .en(demultiplexer_1_out30), .Q(register_31_q), .clk(clock_1_out));  // open: clr
  Register #(.width(32)) register_32 (
    .D(DataD), .en(demultiplexer_1_out31), .Q(register_32_q), .clk(clock_1_out));  // open: clr
  Multiplexer #(.select(5), .width(32)) multiplexer_1 (
    .in0(register_1_q), .in1(register_2_q), .in2(register_3_q), .in3(register_4_q), .in4(register_5_q),
    .in5(register_6_q), .in6(register_7_q), .in7(register_8_q), .in8(register_9_q), .in9(register_10_q),
    .in10(register_11_q), .in11(register_12_q), .in12(register_13_q), .in13(register_14_q),
    .in14(register_15_q), .in15(register_16_q), .in16(register_17_q), .in17(register_18_q),
    .in18(register_19_q), .in19(register_20_q), .in20(register_21_q), .in21(register_22_q),
    .in22(register_23_q), .in23(register_24_q), .in24(register_25_q), .in25(register_26_q),
    .in26(register_27_q), .in27(register_28_q), .in28(register_29_q), .in29(register_30_q),
    .in30(register_31_q), .in31(register_32_q), .out(DataA), .sel(AddrA));  // open: en
  Multiplexer #(.select(5), .width(32)) multiplexer_2 (
    .in0(register_1_q), .in1(register_2_q), .in2(register_3_q), .in3(register_4_q), .in4(register_5_q),
    .in5(register_6_q), .in6(register_7_q), .in7(register_8_q), .in8(register_9_q), .in9(register_10_q),
    .in10(register_11_q), .in11(register_12_q), .in12(register_13_q), .in13(register_14_q),
    .in14(register_15_q), .in15(register_16_q), .in16(register_17_q), .in17(register_18_q),
    .in18(register_19_q), .in19(register_20_q), .in20(register_21_q), .in21(register_22_q),
    .in22(register_23_q), .in23(register_24_q), .in24(register_25_q), .in25(register_26_q),
    .in26(register_27_q), .in27(register_28_q), .in28(register_28_q), .in29(register_30_q),
    .in30(register_31_q), .in31(register_32_q), .out(DataB), .sel(AddrB));  // open: en
  // also tied to GND on the sheet: {register_1_q[0], register_1_q[1], register_1_q[2], register_1_q[3], register_1_q[4], register_1_q[5], register_1_q[6], register_1_q[7], register_1_q[8], register_1_q[9], register_1_q[10], register_1_q[11], register_1_q[12], register_1_q[13], register_1_q[14], register_1_q[15], register_1_q[16], register_1_q[17], register_1_q[18], register_1_q[19], register_1_q[20], register_1_q[21], register_1_q[22], register_1_q[23], register_1_q[24], register_1_q[25], register_1_q[26], register_1_q[27], register_1_q[28], register_1_q[29], register_1_q[30], register_1_q[31]}
endmodule

module Immediate_Generation (
  input  [1:0] Imm_Sel,
  input  [31:0] inst,
  output [31:0] Imm
);

  wire [31:0] bit_extender_1_out, bit_extender_2_out, bit_extender_3_out, bit_extender_4_out;

  assign bit_extender_1_out = {{20{inst[31]}}, inst[31:20]};  // Bit_Extender bit_extender_1
  assign bit_extender_2_out = {{20{inst[31]}}, {inst[31:25], inst[11:7]}};  // Bit_Extender bit_extender_2
  assign bit_extender_3_out = {{19{inst[31]}}, {inst[31], inst[7], inst[30:25], inst[11:8], 1'b0}};  // Bit_Extender bit_extender_3
  assign bit_extender_4_out = {{11{inst[31]}}, {inst[31], inst[19:12], inst[20], inst[30:21], 1'b0}};  // Bit_Extender bit_extender_4
  Multiplexer #(.select(2), .width(32)) multiplexer_1 (
    .in0(bit_extender_1_out), .in1(bit_extender_2_out), .in2(bit_extender_3_out), .in3(bit_extender_4_out),
    .out(Imm), .sel(Imm_Sel));  // open: en

  // Notes on the sheet:
  //   I-Format
  //                 B-Format
  //             S-Format
endmodule

module ALU (
  input  [31:0] A,
  input  [2:0] ALU_Sel,
  input  [31:0] B,
  output [31:0] Result,
  output zero_flag
);

  wire comparator_1_lt;
  wire [31:0] adder_1_out, AND_out, bit_extender_1_out, OR_out, subtractor_1_out, XOR_out;

  Comparator #(.width(32)) comparator_1 (.a(A), .b(B), .lt(comparator_1_lt));  // open: gt, eq
  Adder #(.width(32)) adder_1 (.a(A), .b(B), .out(adder_1_out));  // open: cin, cout
  Subtractor #(.width(32)) subtractor_1 (.a(A), .b(B), .out(subtractor_1_out));  // open: bin, bout
  assign AND_out = A & B;  // AND_Gate AND, 32 bits wide
  assign OR_out = A | B;  // OR_Gate OR, 32 bits wide
  assign XOR_out = A ^ B;  // XOR_Gate XOR, 32 bits wide
  assign bit_extender_1_out = {{31{1'b0}}, comparator_1_lt};  // Bit_Extender bit_extender_1
  Multiplexer #(.select(3), .width(32), .enable("false")) multiplexer_1 (
    .in0(adder_1_out), .in1(subtractor_1_out), .in2(AND_out), .in3(OR_out), .in4(XOR_out),
    .in5(bit_extender_1_out), .out(Result), .sel(ALU_Sel));  // open: in6, in7
  Comparator #(.width(32), .mode("unsigned")) comparator_2 (
    .a(Result), .b({32{1'b0}}), .eq(zero_flag));  // open: gt, lt

  // Notes on the sheet:
  //      STL 
  //   SUB
endmodule

module Branch_Comp (
  input  [31:0] Data_A,
  input  [31:0] Data_B,
  output Br_Eq,
  output Br_LT
);

  Comparator #(.width(32)) comparator_1 (.a(Data_A), .b(Data_B), .eq(Br_Eq), .lt(Br_LT));  // open: gt
endmodule
